# Fritzing sketch Схема 2 (saved by Fritzing 0.9.5d)
breadboards: 1

parts:
  A1 = Orange PI 3 LTS
  Компонент1 = Arduino Uno (Rev3)
  Driver1 = 28BYJ-48 Driver Module [part_number=ULN2003 package=THT]
  SM1 = 28BYJ-48 Stepper Motor [part_number=28BYJ-48]
  Driver2 = 28BYJ-48 Driver Module [part_number=ULN2003 package=THT]  # not connected
  ESP32_-_Back1 = ESP32 - CAM

nets:
  N1: A1.Pin_28, Компонент1.D0/RX, ESP32_-_Back1.GPIO3_/_RX
  N2: A1.Pin_29, Компонент1.D1/TX, ESP32_-_Back1.GPIO1_/_TX
  N3: Компонент1.D2, Driver1.IN1
  N4: Компонент1.D3_PWM, Driver1.IN2
  N5: Компонент1.D4, Driver1.IN3
  N6: Компонент1.D5_PWM, Driver1.IN4
  GND: Компонент1.GND, Driver1.GND
  N7: Driver1.blue-pin, SM1.blue-pin
  N8: Driver1.pink-pin, SM1.pink-pin
  N9: Driver1.yellow-pin, SM1.yellow-pin
  N10: Driver1.orange-pin, SM1.orange-pin
  N11: Driver1.red-pin, SM1.red-pin

custom parts:
  Orange PI 3 LTS: Orange Pi 3 LTS is an open-source single-board computer with dual-band wireless WiFi and Bluetooth 5.0 .It is highly compact with a dimension of 56X85mm.
  28BYJ-48 Driver Module: ULN2003 Driver Module for the 28BYJ-48 Unipolar Stepper Motor LED A - Blue wire - Bottom coil left LED B - Pink wire - Top coil left LED C - Yellow wire - Bottom coil right LED D - Orange wire - Top coil right Common rail - red Connector pins: blue - pink - yellow - orange - red Control pins - IN1 to IN4 Power pins - GND & Vmotor (5-12V) On/Off jumper (if removed, power to motor is cut).
  28BYJ-48 Stepper Motor: Unipolar Stepper Motor 28BYJ-48 Top coil - pink & orange Bottom coil - blue & yellow Common rail - red Connector pins: blue - pink - yellow - orange - red
  ESP32 - CAM: The ESP32-CAM has a very competitive small-size camera module that can operate independently as a minimum system with a footprint of only 27*40.5*4.5mm and a deep sleep current of up to 6mA.
